# Fritzing sketch Dragonfly (saved by Fritzing 0.9.3b)
breadboards: 1

parts:
  DHT1 = DHT11_Temperature_and_Humitidy_Sensor
  Componente1 = Arduino Nano (Rev3.0)
  R1 = Resistor [tolerance=±5% resistance=220 package="2010 [SMD]"]
  Q1 = TIP120 Hi-Current Darlington Transistor [part_number=TIP122]
  Componente2 = FC-28 Soil Hygrometer Module
  Componente3 = FC-28 Soil Hygrometer Module
  Componente4 = FC-28 Soil Hygrometer Module
  Componente5 = FC-28 Soil Hygrometer Module - Probe
  Componente6 = FC-28 Soil Hygrometer Module - Probe
  Componente7 = FC-28 Soil Hygrometer Module - Probe
  Raspberry_Pi_Zero1 = Raspberry Pi Zero
  R2 = Resistor [tolerance=±5% resistance=10 package="2010 [SMD]"]
  R3 = Resistor [tolerance=±5% resistance=22k package="2010 [SMD]"]
  X1 = X113647 Stepper Driver Board [package=board]
  MOTOR1 = 28BYJ-48 Stepper Motor
  R4 = Resistor [tolerance=±5% resistance=2.2 package="2010 [SMD]"]

nets:
  N1: DHT1.connector1, Componente1.D2
  N2: DHT1.connector2, R1.Pin_1
  GND: DHT1.connector4, Componente1.GND, Raspberry_Pi_Zero1.GND, R3.Pin_1, X1.GND
  N3: Componente1.D1/TX, R2.Pin_0
  N4: Componente1.D0/RX, Raspberry_Pi_Zero1.GPIO15, Raspberry_Pi_Zero1.GPIO14, R3.Pin_0
  N5: Componente1.D3, R1.Pin_0
  N6: Componente1.D10, R4.Pin_0
  N7: Componente1.5V, X1.+V
  N8: Componente1.A2, Componente4.AO
  N9: Componente1.A1, Componente3.AO
  N10: Componente1.A0, Componente2.AO
  N11: Q1.BASE, R4.Pin_1
  VCC: Componente2.VCC, Componente3.VCC, Componente4.VCC
  GND_2: Componente2.GND, Componente3.GND, Componente4.GND
  N12: Componente2.POS, Componente5.POS
  N13: Componente2.NEG, Componente5.NEG
  N14: Componente3.POS, Componente6.POS
  N15: Componente3.NEG, Componente6.NEG
  N16: Componente4.POS, Componente7.POS
  N17: Componente4.NEG, Componente7.NEG
  N18: Raspberry_Pi_Zero1.GPIO4, X1.IN1
  N19: Raspberry_Pi_Zero1.GPIO17, X1.IN2
  N20: Raspberry_Pi_Zero1.GPIO27, X1.IN3
  N21: Raspberry_Pi_Zero1.GPIO22, X1.IN4
  N22: X1.BLUE, MOTOR1.BLUE
  N23: X1.PINK, MOTOR1.PINK
  N24: X1.YELLOW, MOTOR1.RED
  N25: X1.ORANGE, MOTOR1.ORANGE
  N26: X1.RED, MOTOR1.YELLOW

custom parts:
  FC-28 Soil Hygrometer Module: The FC-28 is a soil hygrometer module that uses the Texas Instruments LM393 comparator chip to provide an analog measurement of soil humidity. The digital output is high when soil moisture is over a certain threshold, as determined by adjusting the potentiometer.
  FC-28 Soil Hygrometer Module - Probe: The FC-28 is a soil hygrometer module that uses the Texas Instruments LM393 comparator chip to provide an analog measurement of soil humidity.
  X113647 Stepper Driver Board: A common stepper motor driver board based on ULN2003APG darlington array
  28BYJ-48 Stepper Motor: 28BYJ-48 gear-reduction stepper motor (small)
